// Logisim project 1d_8-bit_CAS.circ as structural Verilog: 1 circuit, main circuit 1d: n-Bit-CAS
module _1d__n_Bit_CAS (
  input  Add,
  input  a1,
  input  b1,
  input  a2,
  input  b2,
  input  a3,
  input  b3,
  input  a4,
  input  b4,
  input  a5,
  input  b5,
  input  a6,
  input  b6,
  input  a7,
  input  b7,
  input  a8,
  input  b8,
  output s1,
  output s2,
  output s3,
  output s4,
  output s5,
  output s6,
  output s7,
  output s8
);

  wire n1b_adder_1_ci, n1b_adder_2_ci, n1b_adder_3_ci, n1b_adder_4_ci, n1b_adder_5_ci, n1b_adder_6_ci,
       n1b_adder_7_ci, n1b_adder_8_ci, n1c_transmissions_1_f_x_y, n1c_transmissions_2_f_x_y,
       n1c_transmissions_3_f_x_y, n1c_transmissions_4_f_x_y, n1c_transmissions_5_f_x_y,
       n1c_transmissions_6_f_x_y, n1c_transmissions_7_f_x_y, n1c_transmissions_8_f_x_y,
       n1c_transmissions_9_f_x_y;

  _1c__Transmission_Gates u_1c_transmissions_1 (.y(1'b0), .x(Add), .f_x_y(n1c_transmissions_1_f_x_y));
  _1c__Transmission_Gates u_1c_transmissions_2 (.y(Add), .x(b1), .f_x_y(n1c_transmissions_2_f_x_y));
  _1c__Transmission_Gates u_1c_transmissions_3 (.y(Add), .x(b2), .f_x_y(n1c_transmissions_3_f_x_y));
  _1c__Transmission_Gates u_1c_transmissions_4 (.y(Add), .x(b3), .f_x_y(n1c_transmissions_4_f_x_y));
  _1c__Transmission_Gates u_1c_transmissions_5 (.y(Add), .x(b4), .f_x_y(n1c_transmissions_5_f_x_y));
  _1c__Transmission_Gates u_1c_transmissions_6 (.y(Add), .x(b5), .f_x_y(n1c_transmissions_6_f_x_y));
  _1c__Transmission_Gates u_1c_transmissions_7 (.y(Add), .x(b6), .f_x_y(n1c_transmissions_7_f_x_y));
  _1c__Transmission_Gates u_1c_transmissions_8 (.y(Add), .x(b7), .f_x_y(n1c_transmissions_8_f_x_y));
  _1c__Transmission_Gates u_1c_transmissions_9 (.y(Add), .x(b8), .f_x_y(n1c_transmissions_9_f_x_y));
  _1b__Adder u_1b_adder_1 (
    .Ai(a1), .Bi(n1c_transmissions_2_f_x_y), .Ci_1(n1c_transmissions_1_f_x_y), .Si(s1), .Ci(n1b_adder_1_ci));
  _1b__Adder u_1b_adder_2 (
    .Ai(a2), .Bi(n1c_transmissions_3_f_x_y), .Ci_1(n1b_adder_1_ci), .Si(s2), .Ci(n1b_adder_2_ci));
  _1b__Adder u_1b_adder_3 (
    .Ai(a3), .Bi(n1c_transmissions_4_f_x_y), .Ci_1(n1b_adder_2_ci), .Si(s3), .Ci(n1b_adder_3_ci));
  _1b__Adder u_1b_adder_4 (
    .Ai(a4), .Bi(n1c_transmissions_5_f_x_y), .Ci_1(n1b_adder_3_ci), .Si(s4), .Ci(n1b_adder_4_ci));
  _1b__Adder u_1b_adder_5 (
    .Ai(a5), .Bi(n1c_transmissions_6_f_x_y), .Ci_1(n1b_adder_4_ci), .Si(s5), .Ci(n1b_adder_5_ci));
  _1b__Adder u_1b_adder_6 (
    .Ai(a6), .Bi(n1c_transmissions_7_f_x_y), .Ci_1(n1b_adder_5_ci), .Si(s6), .Ci(n1b_adder_6_ci));
  _1b__Adder u_1b_adder_7 (
    .Ai(a7), .Bi(n1c_transmissions_8_f_x_y), .Ci_1(n1b_adder_6_ci), .Si(s7), .Ci(n1b_adder_7_ci));
  _1b__Adder u_1b_adder_8 (
    .Ai(a8), .Bi(n1c_transmissions_9_f_x_y), .Ci_1(n1b_adder_7_ci), .Si(s8), .Ci(n1b_adder_8_ci));
endmodule
