// Logisim project 1b_CMOS_FullAdder.circ as structural Verilog: 1 circuit, main circuit 1b: Adder
module _1b__Adder (
  input  Ai,
  input  Bi,
  input  Ci_1,
  output Si,
  output Ci
);

  wire nCi, nSi, transistor_1_out, transistor_2_out, transistor_5_out, transistor_10_out, transistor_11_out,
       transistor_15_out, transistor_18_out, transistor_19_out, transistor_24_out, transistor_26_out;

  Transistor transistor_1 (.in(1'b1), .out(transistor_1_out), .gate(Ai));
  Transistor #(.\type ("n")) transistor_2 (.in(1'b0), .out(transistor_2_out), .gate(Ai));
  Transistor transistor_3 (.in(1'b1), .out(transistor_1_out), .gate(Bi));
  Transistor transistor_4 (.in(transistor_1_out), .out(nCi), .gate(Ci_1));
  Transistor transistor_5 (.in(transistor_1_out), .out(transistor_5_out), .gate(Ai));
  Transistor transistor_6 (.in(transistor_5_out), .out(nCi), .gate(Bi));
  Transistor #(.\type ("n")) transistor_7 (.in(transistor_2_out), .out(nCi), .gate(Ci_1));
  Transistor #(.\type ("n")) transistor_8 (.in(1'b0), .out(transistor_2_out), .gate(Bi));
  Transistor #(.\type ("n")) transistor_9 (.in(transistor_10_out), .out(nCi), .gate(Bi));
  Transistor #(.\type ("n")) transistor_10 (.in(1'b0), .out(transistor_10_out), .gate(Ai));
  Transistor transistor_11 (.in(1'b1), .out(transistor_11_out), .gate(Ai));
  Transistor transistor_12 (.in(1'b1), .out(transistor_11_out), .gate(Bi));
  Transistor transistor_13 (.in(transistor_11_out), .out(nSi), .gate(nCi));
  Transistor #(.\type ("n")) transistor_14 (.in(transistor_15_out), .out(nSi), .gate(nCi));
  Transistor #(.\type ("n")) transistor_15 (.in(1'b0), .out(transistor_15_out), .gate(Bi));
  Transistor #(.\type ("n")) transistor_16 (.in(1'b0), .out(transistor_15_out), .gate(Ai));
  Transistor transistor_17 (.in(1'b1), .out(transistor_11_out), .gate(Ci_1));
  Transistor transistor_18 (.in(transistor_11_out), .out(transistor_18_out), .gate(Ci_1));
  Transistor transistor_19 (.in(transistor_18_out), .out(transistor_19_out), .gate(Bi));
  Transistor transistor_20 (.in(transistor_19_out), .out(nSi), .gate(Ai));
  Transistor #(.\type ("n")) transistor_21 (.in(1'b0), .out(transistor_15_out), .gate(Ci_1));
  Transistor transistor_22 (.in(1'b1), .out(Ci), .gate(nCi));
  Transistor #(.\type ("n")) transistor_23 (.in(transistor_24_out), .out(nSi), .gate(Ci_1));
  Transistor #(.\type ("n")) transistor_24 (.in(transistor_26_out), .out(transistor_24_out), .gate(Bi));
  Transistor #(.\type ("n")) transistor_25 (.in(1'b0), .out(Ci), .gate(nCi));
  Transistor #(.\type ("n")) transistor_26 (.in(1'b0), .out(transistor_26_out), .gate(Ai));
  Transistor transistor_27 (.in(1'b1), .out(Si), .gate(nSi));
  Transistor #(.\type ("n")) transistor_28 (.in(1'b0), .out(Si), .gate(nSi));
endmodule
