// Logisim project 1c_Transmission_Gates.circ as structural Verilog: 1 circuit, main circuit 1c: Transmission Gates
module _1c__Transmission_Gates (
  input  y,
  input  x,
  output f_x_y
);

  wire and_1_out, not_2_out, not_3_out, or_1_out, or_2_out, transistor_1_out, transistor_3_out,
       transistor_4_out, transistor_7_out, transistor_8_out, transistor_11_out, transistor_12_out,
       transistor_15_out, transistor_17_out, transistor_21_out, transistor_22_out, transistor_24_out,
       transistor_25_out, transistor_28_out, transistor_29_out, transistor_30_out, transistor_32_out,
       transistor_33_out, transistor_36_out, transistor_37_out, transistor_40_out, transistor_41_out,
       transistor_45_out, transmission_1_p1, transmission_1_p3;

  Transistor transistor_1 (.in(1'b1), .out(transistor_1_out), .gate(y));
  Transistor #(.\type ("n")) transistor_2 (.in(1'b0), .out(transistor_1_out), .gate(y));
  // Transmission_Gate transmission_1: pin names not known; wires that end beside it: transmission_1_p1, y, transmission_1_p3
  not not_1 (transmission_1_p1, x);
  not not_2 (not_2_out, y);
  // Transmission_Gate transmission_2: pin names not known; wires that end beside it: x, not_2_out, y, transmission_1_p3, transmission_1_p3
  Transistor transistor_3 (.in(1'b1), .out(transistor_3_out), .gate(y));
  Transistor transistor_4 (.in(1'b1), .out(transistor_4_out), .gate(x));
  Transistor #(.\type ("n")) transistor_5 (.in(1'b0), .out(transistor_4_out), .gate(x));
  Transistor #(.\type ("n")) transistor_6 (.in(1'b0), .out(transistor_3_out), .gate(y));
  Transistor transistor_7 (.in(1'b1), .out(transistor_7_out), .gate(y));
  Transistor transistor_8 (.in(1'b1), .out(transistor_8_out), .gate(x));
  Transistor #(.\type ("n")) transistor_9 (.in(1'b0), .out(transistor_7_out), .gate(y));
  Transistor #(.\type ("n")) transistor_10 (.in(1'b0), .out(transistor_8_out), .gate(x));
  Transistor transistor_11 (.in(1'b1), .out(transistor_11_out), .gate(y));
  Transistor transistor_12 (.in(1'b1), .out(transistor_12_out), .gate(x));
  Transistor #(.\type ("n")) transistor_13 (.in(1'b0), .out(transistor_12_out), .gate(x));
  Transistor #(.\type ("n")) transistor_14 (.in(1'b0), .out(transistor_11_out), .gate(y));
  Transistor transistor_15 (.in(1'b1), .out(transistor_15_out), .gate(x));
  Transistor #(.\type ("n")) transistor_16 (.in(1'b0), .out(transistor_15_out), .gate(x));
  Transistor transistor_17 (.in(transistor_4_out), .out(transistor_17_out), .gate(y));
  Transistor #(.\type ("n"), .gate("br")) transistor_18 (
    .in(transistor_4_out), .out(transistor_17_out), .gate(transistor_3_out));
  Transistor transistor_19 (.in(x), .out(transistor_17_out), .gate(transistor_3_out));
  Transistor #(.\type ("n"), .gate("br")) transistor_20 (.in(x), .out(transistor_17_out), .gate(y));
  Transistor transistor_21 (.in(1'b1), .out(transistor_21_out), .gate(y));
  Transistor transistor_22 (.in(transistor_21_out), .out(transistor_22_out), .gate(transistor_8_out));
  Transistor #(.\type ("n")) transistor_23 (.in(transistor_24_out), .out(transistor_22_out), .gate(y));
  Transistor #(.\type ("n")) transistor_24 (.in(1'b0), .out(transistor_24_out), .gate(x));
  Transistor transistor_25 (.in(1'b1), .out(transistor_25_out), .gate(x));
  Transistor transistor_26 (.in(transistor_25_out), .out(f_x_y), .gate(y));
  Transistor #(.\type ("n")) transistor_27 (.in(transistor_28_out), .out(f_x_y), .gate(transistor_12_out));
  Transistor #(.\type ("n")) transistor_28 (.in(1'b0), .out(transistor_28_out), .gate(y));
  Transistor transistor_29 (.in(1'b1), .out(transistor_29_out), .gate(y));
  Transistor transistor_30 (.in(transistor_29_out), .out(transistor_30_out), .gate(x));
  Transistor #(.\type ("n")) transistor_31 (.in(transistor_32_out), .out(transistor_30_out), .gate(y));
  Transistor #(.\type ("n")) transistor_32 (.in(1'b0), .out(transistor_32_out), .gate(transistor_15_out));
  Transistor transistor_33 (.in(1'b1), .out(transistor_33_out), .gate(transistor_7_out));
  Transistor transistor_34 (.in(transistor_33_out), .out(transistor_22_out), .gate(x));
  Transistor #(.\type ("n")) transistor_35 (.in(transistor_36_out), .out(transistor_22_out), .gate(transistor_7_out));
  Transistor #(.\type ("n")) transistor_36 (.in(1'b0), .out(transistor_36_out), .gate(transistor_8_out));
  Transistor transistor_37 (.in(1'b1), .out(transistor_37_out), .gate(transistor_11_out));
  Transistor transistor_38 (.in(transistor_37_out), .out(f_x_y), .gate(transistor_12_out));
  Transistor #(.\type ("n")) transistor_39 (.in(transistor_40_out), .out(f_x_y), .gate(x));
  Transistor #(.\type ("n")) transistor_40 (.in(1'b0), .out(transistor_40_out), .gate(transistor_11_out));
  Transistor transistor_41 (.in(1'b1), .out(transistor_41_out), .gate(transistor_1_out));
  Transistor transistor_42 (.in(transistor_41_out), .out(transistor_30_out), .gate(transistor_15_out));
  Transistor #(.\type ("n")) transistor_43 (.in(transistor_32_out), .out(transistor_30_out), .gate(x));
  Transistor #(.\type ("n")) transistor_44 (.in(1'b0), .out(transistor_32_out), .gate(transistor_1_out));
  Transistor transistor_45 (.in(1'b1), .out(transistor_45_out), .gate(transistor_22_out));
  Transistor #(.\type ("n")) transistor_46 (.in(1'b0), .out(transistor_45_out), .gate(transistor_22_out));
  and and_1 (and_1_out, y, x);
  or or_1 (or_1_out, x, y);
  not not_3 (not_3_out, or_1_out);
  or or_2 (or_2_out, and_1_out, not_3_out);

  // Notes on the sheet:
  //   Angabe
  //   Angabe nur mit Transistoren
  //   CMOS-XOR aus Vorlesung => XOR
  //   Identisch, aber basierend auf Gleichheits-Formel, nach CMOS vorgehen
  //   CMOS-XOR aus Vorlesung + Inverter => XNOR
  //   ABER: PUN und PDN Vertauscht! => XNOR
  //   I) Schaltdiagramm implementiert (y*!x)+(!y*x)
  //   => Gleichheit
  //   II) 8 Transistoren
  //   III) 12 Transistoren
endmodule
