// Logisim project Praktikum_LogisimEvolution_Woche1.circ as structural Verilog
module L_1b_Adder (
  input  Ai,
  input  Bi,
  input  Ci_1,
  output Si,
  output Ci
);

  wire NOT_Ci, NOT_Si, transistor_1_out, transistor_2_out, transistor_5_out, transistor_10_out,
       transistor_11_out, transistor_15_out, transistor_18_out, transistor_19_out, transistor_23_out,
       transistor_24_out;

  Transistor transistor_1 (.in(1'b1), .out(transistor_1_out), .gate(Ai));
  Transistor #(.\type ("n")) transistor_2 (.in(1'b0), .out(transistor_2_out), .gate(Ai));
  Transistor transistor_3 (.in(1'b1), .out(transistor_1_out), .gate(Bi));
  Transistor transistor_4 (.in(transistor_1_out), .out(NOT_Ci), .gate(Ci_1));
  Transistor transistor_5 (.in(transistor_1_out), .out(transistor_5_out), .gate(Ai));
  Transistor transistor_6 (.in(transistor_5_out), .out(NOT_Ci), .gate(Bi));
  Transistor #(.\type ("n")) transistor_7 (.in(transistor_2_out), .out(NOT_Ci), .gate(Ci_1));
  Transistor #(.\type ("n")) transistor_8 (.in(1'b0), .out(transistor_2_out), .gate(Bi));
  Transistor #(.\type ("n")) transistor_9 (.in(transistor_10_out), .out(NOT_Ci), .gate(Bi));
  Transistor #(.\type ("n")) transistor_10 (.in(1'b0), .out(transistor_10_out), .gate(Ai));
  Transistor transistor_11 (.in(1'b1), .out(transistor_11_out), .gate(Ai));
  Transistor transistor_12 (.in(1'b1), .out(transistor_11_out), .gate(Bi));
  Transistor transistor_13 (.in(transistor_11_out), .out(NOT_Si), .gate(NOT_Ci));
  Transistor #(.\type ("n")) transistor_14 (.in(transistor_15_out), .out(NOT_Si), .gate(NOT_Ci));
  Transistor #(.\type ("n")) transistor_15 (.in(1'b0), .out(transistor_15_out), .gate(Ai));
  Transistor #(.\type ("n")) transistor_16 (.in(1'b0), .out(transistor_15_out), .gate(Bi));
  Transistor transistor_17 (.in(1'b1), .out(transistor_11_out), .gate(Ci_1));
  Transistor transistor_18 (.in(transistor_11_out), .out(transistor_18_out), .gate(Ci_1));
  Transistor transistor_19 (.in(transistor_18_out), .out(transistor_19_out), .gate(Bi));
  Transistor transistor_20 (.in(transistor_19_out), .out(NOT_Si), .gate(Ai));
  Transistor #(.\type ("n")) transistor_21 (.in(1'b0), .out(transistor_15_out), .gate(Ci_1));
  Transistor #(.\type ("n")) transistor_22 (.in(transistor_23_out), .out(NOT_Si), .gate(Ci_1));
  Transistor #(.\type ("n")) transistor_23 (.in(transistor_24_out), .out(transistor_23_out), .gate(Bi));
  Transistor #(.\type ("n")) transistor_24 (.in(1'b0), .out(transistor_24_out), .gate(Ai));
  Transistor transistor_25 (.in(1'b1), .out(Ci), .gate(NOT_Ci));
  Transistor #(.\type ("n")) transistor_26 (.in(1'b0), .out(Ci), .gate(NOT_Ci));
  Transistor transistor_27 (.in(1'b1), .out(Si), .gate(NOT_Si));
  Transistor #(.\type ("n")) transistor_28 (.in(1'b0), .out(Si), .gate(NOT_Si));
endmodule

module L_1c_Transmission_Gates (
  input  y,
  input  x,
  output f_x_y
);

  wire and_1_out, not_2_out, not_3_out, or_1_out, or_2_out, transistor_1_out, transistor_3_out,
       transistor_4_out, transistor_7_out, transistor_8_out, transistor_11_out, transistor_12_out,
       transistor_15_out, transistor_17_out, transistor_21_out, transistor_22_out, transistor_24_out,
       transistor_25_out, transistor_28_out, transistor_29_out, transistor_30_out, transistor_32_out,
       transistor_33_out, transistor_36_out, transistor_37_out, transistor_40_out, transistor_41_out,
       transistor_45_out, transistor_47_out, transistor_48_out, transistor_51_out, transistor_52_out,
       transistor_54_out, transistor_55_out, transmission_1_p1, transmission_1_p3;

  Transistor transistor_1 (.in(1'b1), .out(transistor_1_out), .gate(y));
  Transistor #(.\type ("n")) transistor_2 (.in(1'b0), .out(transistor_1_out), .gate(y));
  // Transmission_Gate transmission_1: pin names not known; wires that end beside it: transmission_1_p1, y, transmission_1_p3
  not not_1 (transmission_1_p1, x);
  not not_2 (not_2_out, y);
  // Transmission_Gate transmission_2: pin names not known; wires that end beside it: x, not_2_out, y, transmission_1_p3, transmission_1_p3
  Transistor transistor_3 (.in(1'b1), .out(transistor_3_out), .gate(y));
  Transistor transistor_4 (.in(1'b1), .out(transistor_4_out), .gate(x));
  Transistor #(.\type ("n")) transistor_5 (.in(1'b0), .out(transistor_3_out), .gate(y));
  Transistor #(.\type ("n")) transistor_6 (.in(1'b0), .out(transistor_4_out), .gate(x));
  Transistor transistor_7 (.in(1'b1), .out(transistor_7_out), .gate(y));
  Transistor transistor_8 (.in(1'b1), .out(transistor_8_out), .gate(x));
  Transistor #(.\type ("n")) transistor_9 (.in(1'b0), .out(transistor_7_out), .gate(y));
  Transistor #(.\type ("n")) transistor_10 (.in(1'b0), .out(transistor_8_out), .gate(x));
  Transistor transistor_11 (.in(1'b1), .out(transistor_11_out), .gate(y));
  Transistor transistor_12 (.in(1'b1), .out(transistor_12_out), .gate(x));
  Transistor #(.\type ("n")) transistor_13 (.in(1'b0), .out(transistor_11_out), .gate(y));
  Transistor #(.\type ("n")) transistor_14 (.in(1'b0), .out(transistor_12_out), .gate(x));
  Transistor transistor_15 (.in(1'b1), .out(transistor_15_out), .gate(x));
  Transistor #(.\type ("n")) transistor_16 (.in(1'b0), .out(transistor_15_out), .gate(x));
  Transistor transistor_17 (.in(transistor_4_out), .out(transistor_17_out), .gate(y));
  Transistor #(.\type ("n")) transistor_18 (.in(transistor_4_out), .out(transistor_17_out), .gate(transistor_3_out));
  Transistor transistor_19 (.in(x), .out(transistor_17_out), .gate(transistor_3_out));
  Transistor #(.\type ("n")) transistor_20 (.in(x), .out(transistor_17_out), .gate(y));
  Transistor transistor_21 (.in(1'b1), .out(transistor_21_out), .gate(y));
  Transistor transistor_22 (.in(transistor_21_out), .out(transistor_22_out), .gate(transistor_8_out));
  Transistor #(.\type ("n")) transistor_23 (.in(transistor_24_out), .out(transistor_22_out), .gate(y));
  Transistor #(.\type ("n")) transistor_24 (.in(1'b0), .out(transistor_24_out), .gate(x));
  Transistor transistor_25 (.in(1'b1), .out(transistor_25_out), .gate(x));
  Transistor transistor_26 (.in(transistor_25_out), .out(f_x_y), .gate(y));
  Transistor #(.\type ("n")) transistor_27 (.in(transistor_28_out), .out(f_x_y), .gate(transistor_12_out));
  Transistor #(.\type ("n")) transistor_28 (.in(1'b0), .out(transistor_28_out), .gate(y));
  Transistor transistor_29 (.in(1'b1), .out(transistor_29_out), .gate(y));
  Transistor transistor_30 (.in(transistor_29_out), .out(transistor_30_out), .gate(x));
  Transistor #(.\type ("n")) transistor_31 (.in(transistor_32_out), .out(transistor_30_out), .gate(y));
  Transistor #(.\type ("n")) transistor_32 (.in(1'b0), .out(transistor_32_out), .gate(transistor_15_out));
  Transistor transistor_33 (.in(1'b1), .out(transistor_33_out), .gate(transistor_7_out));
  Transistor transistor_34 (.in(transistor_33_out), .out(transistor_22_out), .gate(x));
  Transistor #(.\type ("n")) transistor_35 (.in(transistor_36_out), .out(transistor_22_out), .gate(transistor_7_out));
  Transistor #(.\type ("n")) transistor_36 (.in(1'b0), .out(transistor_36_out), .gate(transistor_8_out));
  Transistor transistor_37 (.in(1'b1), .out(transistor_37_out), .gate(transistor_11_out));
  Transistor transistor_38 (.in(transistor_37_out), .out(f_x_y), .gate(transistor_12_out));
  Transistor #(.\type ("n")) transistor_39 (.in(transistor_40_out), .out(f_x_y), .gate(x));
  Transistor #(.\type ("n")) transistor_40 (.in(1'b0), .out(transistor_40_out), .gate(transistor_11_out));
  Transistor transistor_41 (.in(1'b1), .out(transistor_41_out), .gate(transistor_1_out));
  Transistor transistor_42 (.in(transistor_41_out), .out(transistor_30_out), .gate(transistor_15_out));
  Transistor #(.\type ("n")) transistor_43 (.in(transistor_32_out), .out(transistor_30_out), .gate(x));
  Transistor #(.\type ("n")) transistor_44 (.in(1'b0), .out(transistor_32_out), .gate(transistor_1_out));
  Transistor transistor_45 (.in(1'b1), .out(transistor_45_out), .gate(transistor_22_out));
  Transistor #(.\type ("n")) transistor_46 (.in(1'b0), .out(transistor_45_out), .gate(transistor_22_out));
  and and_1 (and_1_out, y, x);
  or or_1 (or_1_out, x, y);
  not not_3 (not_3_out, or_1_out);
  Transistor transistor_47 (.in(1'b1), .out(transistor_47_out), .gate(y));
  Transistor transistor_48 (.in(1'b1), .out(transistor_48_out), .gate(x));
  Transistor #(.\type ("n")) transistor_49 (.in(1'b0), .out(transistor_47_out), .gate(y));
  Transistor #(.\type ("n")) transistor_50 (.in(1'b0), .out(transistor_48_out), .gate(x));
  or or_2 (or_2_out, and_1_out, not_3_out);
  Transistor transistor_51 (.in(1'b1), .out(transistor_51_out), .gate(x));
  Transistor transistor_52 (.in(transistor_51_out), .out(transistor_52_out), .gate(y));
  Transistor #(.\type ("n")) transistor_53 (.in(transistor_54_out), .out(transistor_52_out), .gate(y));
  Transistor #(.\type ("n")) transistor_54 (.in(1'b0), .out(transistor_54_out), .gate(transistor_48_out));
  // XNOR_Gate xnor_1 is placed but not wired
  Transistor transistor_55 (.in(1'b1), .out(transistor_55_out), .gate(transistor_48_out));
  Transistor transistor_56 (.in(transistor_55_out), .out(transistor_52_out), .gate(transistor_47_out));
  Transistor #(.\type ("n")) transistor_57 (.in(transistor_54_out), .out(transistor_52_out), .gate(x));
  Transistor #(.\type ("n")) transistor_58 (.in(1'b0), .out(transistor_54_out), .gate(transistor_47_out));

  // Notes on the sheet:
  //   Angabe
  //   Angabe nur mit Transistoren
  //   CMOS-XOR aus Vorlesung => XOR
  //   CMOS-XOR aus Vorlesung + Inverter => XNOR
  //   ABER: PUN und PDN Vertauscht! => XNOR
  //   Identisch, aber basierend auf Gleichheits-Formel, nach CMOS vorgehen
  //   I) Schaltdiagramm implementiert (y*!x)+(!y*x)
  //   => Gleichheit
  //   II) 8 Transistoren
  //   III) 12 Transistoren
  //   XNOR/Equals
endmodule

module L_1d_n_Bit_CAS (
  input  Add,
  input  a1,
  input  b1,
  input  a2,
  input  b2,
  input  a3,
  input  b3,
  input  a4,
  input  b4,
  input  a5,
  input  b5,
  input  a6,
  input  b6,
  input  a7,
  input  b7,
  input  a8,
  input  b8,
  output s1,
  output s2,
  output s3,
  output s4,
  output s5,
  output s6,
  output s7,
  output s8
);

  wire l_1b_adder_1_ci, l_1b_adder_2_ci, l_1b_adder_3_ci, l_1b_adder_4_ci, l_1b_adder_5_ci, l_1b_adder_6_ci,
       l_1b_adder_7_ci, l_1b_adder_8_ci, l_1c_transmission_gates_1_f_x_y, l_1c_transmission_gates_2_f_x_y,
       l_1c_transmission_gates_3_f_x_y, l_1c_transmission_gates_4_f_x_y, l_1c_transmission_gates_5_f_x_y,
       l_1c_transmission_gates_6_f_x_y, l_1c_transmission_gates_7_f_x_y, l_1c_transmission_gates_8_f_x_y,
       l_1c_transmission_gates_9_f_x_y;

  L_1c_Transmission_Gates l_1c_transmission_gates_1 (.f_x_y(l_1c_transmission_gates_1_f_x_y), .y(1'b0), .x(Add));
  L_1c_Transmission_Gates l_1c_transmission_gates_2 (.f_x_y(l_1c_transmission_gates_2_f_x_y), .y(Add), .x(b1));
  L_1c_Transmission_Gates l_1c_transmission_gates_3 (.f_x_y(l_1c_transmission_gates_3_f_x_y), .y(Add), .x(b2));
  L_1c_Transmission_Gates l_1c_transmission_gates_4 (.f_x_y(l_1c_transmission_gates_4_f_x_y), .y(Add), .x(b3));
  L_1c_Transmission_Gates l_1c_transmission_gates_5 (.f_x_y(l_1c_transmission_gates_5_f_x_y), .y(Add), .x(b4));
  L_1c_Transmission_Gates l_1c_transmission_gates_6 (.f_x_y(l_1c_transmission_gates_6_f_x_y), .y(Add), .x(b5));
  L_1c_Transmission_Gates l_1c_transmission_gates_7 (.f_x_y(l_1c_transmission_gates_7_f_x_y), .y(Add), .x(b6));
  L_1c_Transmission_Gates l_1c_transmission_gates_8 (.f_x_y(l_1c_transmission_gates_8_f_x_y), .y(Add), .x(b7));
  L_1c_Transmission_Gates l_1c_transmission_gates_9 (.f_x_y(l_1c_transmission_gates_9_f_x_y), .y(Add), .x(b8));
  L_1b_Adder l_1b_adder_1 (
    .Si(s1), .Ci(l_1b_adder_1_ci), .Ai(a1), .Bi(l_1c_transmission_gates_2_f_x_y),
    .Ci_1(l_1c_transmission_gates_1_f_x_y));
  L_1b_Adder l_1b_adder_2 (
    .Si(s2), .Ci(l_1b_adder_2_ci), .Ai(a2), .Bi(l_1c_transmission_gates_3_f_x_y), .Ci_1(l_1b_adder_1_ci));
  L_1b_Adder l_1b_adder_3 (
    .Si(s3), .Ci(l_1b_adder_3_ci), .Ai(a3), .Bi(l_1c_transmission_gates_4_f_x_y), .Ci_1(l_1b_adder_2_ci));
  L_1b_Adder l_1b_adder_4 (
    .Si(s4), .Ci(l_1b_adder_4_ci), .Ai(a4), .Bi(l_1c_transmission_gates_5_f_x_y), .Ci_1(l_1b_adder_3_ci));
  L_1b_Adder l_1b_adder_5 (
    .Si(s5), .Ci(l_1b_adder_5_ci), .Ai(a5), .Bi(l_1c_transmission_gates_6_f_x_y), .Ci_1(l_1b_adder_4_ci));
  L_1b_Adder l_1b_adder_6 (
    .Si(s6), .Ci(l_1b_adder_6_ci), .Ai(a6), .Bi(l_1c_transmission_gates_7_f_x_y), .Ci_1(l_1b_adder_5_ci));
  L_1b_Adder l_1b_adder_7 (
    .Si(s7), .Ci(l_1b_adder_7_ci), .Ai(a7), .Bi(l_1c_transmission_gates_8_f_x_y), .Ci_1(l_1b_adder_6_ci));
  L_1b_Adder l_1b_adder_8 (
    .Si(s8), .Ci(l_1b_adder_8_ci), .Ai(a8), .Bi(l_1c_transmission_gates_9_f_x_y), .Ci_1(l_1b_adder_7_ci));
endmodule

module L_2a_Wellenform_Diagramm (
  input  R,
  input  S,
  output Q,
  output NOT_Q
);

  nor nor_1 (Q, R, NOT_Q);
  nor nor_2 (NOT_Q, Q, S);

  // Notes on the sheet:
  //   R
  //   S
  //   Q
  //   !Q
  //   0
  //   20
  //   60
  //   80
  //   40
  //   120
  //   140
  //   160
  //   100
  //   240
  //   200
  //   220
  //   180
  //   t[ns]
  //   260
  //   280
endmodule

module L_2b_D_Flipfolp (
  input  Data,
  input  Enable,
  input  Clock,
  input  Set,
  input  Reset,
  output Q,
  output NOT_Q
);

  wire and_1_out, and_2_out, and_3_out, buffer_1_out, buffer_2_out, nor_1_out, not_1_out, not_2_out,
       or_1_out, or_2_out;

  buf buffer_1 (buffer_1_out, Clock);
  not not_1 (not_1_out, buffer_1_out);
  not not_2 (not_2_out, Data);
  buf buffer_2 (buffer_2_out, Data);
  nor nor_1 (nor_1_out, not_1_out, Clock);
  and and_1 (and_1_out, not_2_out, and_3_out);
  and and_2 (and_2_out, buffer_2_out, and_3_out);
  and and_3 (and_3_out, Enable, nor_1_out);
  or or_1 (or_1_out, and_1_out, Reset);
  or or_2 (or_2_out, and_2_out, Set);
  L_2a_Wellenform_Diagramm l_2a_wellenform_diagramm_1 (.NOT_Q(NOT_Q), .Q(Q), .S(or_2_out), .R(or_1_out));
endmodule

module L_2c_n_Bit_Register (
  input  Reset,
  input  Set,
  input  Enable,
  input  CLK,
  input  Data1,
  input  Data2,
  input  Data3,
  input  Data4,
  input  Data5,
  input  Data6,
  input  Data7,
  input  Data8,
  output Out1,
  output Out2,
  output Out3,
  output Out4,
  output Out5,
  output Out6,
  output Out7,
  output Out8
);

  wire l_2b_d_flipfolp_1_not_q, l_2b_d_flipfolp_2_not_q, l_2b_d_flipfolp_3_not_q, l_2b_d_flipfolp_4_not_q,
       l_2b_d_flipfolp_5_not_q, l_2b_d_flipfolp_6_not_q, l_2b_d_flipfolp_7_not_q, l_2b_d_flipfolp_8_not_q;

  L_2b_D_Flipfolp l_2b_d_flipfolp_1 (
    .Q(Out1), .NOT_Q(l_2b_d_flipfolp_1_not_q), .Clock(CLK), .Data(Data1), .Enable(Enable), .Set(Set),
    .Reset(Reset));
  L_2b_D_Flipfolp l_2b_d_flipfolp_2 (
    .Q(Out2), .NOT_Q(l_2b_d_flipfolp_2_not_q), .Clock(CLK), .Data(Data2), .Enable(Enable), .Set(Set),
    .Reset(Reset));
  L_2b_D_Flipfolp l_2b_d_flipfolp_3 (
    .Q(Out3), .NOT_Q(l_2b_d_flipfolp_3_not_q), .Clock(CLK), .Data(Data3), .Enable(Enable), .Set(Set),
    .Reset(Reset));
  L_2b_D_Flipfolp l_2b_d_flipfolp_4 (
    .Q(Out4), .NOT_Q(l_2b_d_flipfolp_4_not_q), .Clock(CLK), .Data(Data4), .Enable(Enable), .Set(Set),
    .Reset(Reset));
  L_2b_D_Flipfolp l_2b_d_flipfolp_5 (
    .Q(Out5), .NOT_Q(l_2b_d_flipfolp_5_not_q), .Clock(CLK), .Data(Data5), .Enable(Enable), .Set(Set),
    .Reset(Reset));
  L_2b_D_Flipfolp l_2b_d_flipfolp_6 (
    .Q(Out6), .NOT_Q(l_2b_d_flipfolp_6_not_q), .Clock(CLK), .Data(Data6), .Enable(Enable), .Set(Set),
    .Reset(Reset));
  L_2b_D_Flipfolp l_2b_d_flipfolp_7 (
    .Q(Out7), .NOT_Q(l_2b_d_flipfolp_7_not_q), .Clock(CLK), .Data(Data7), .Enable(Enable), .Set(Set),
    .Reset(Reset));
  L_2b_D_Flipfolp l_2b_d_flipfolp_8 (
    .Q(Out8), .NOT_Q(l_2b_d_flipfolp_8_not_q), .Clock(CLK), .Data(Data8), .Enable(Enable), .Set(Set),
    .Reset(Reset));
endmodule

module L_2c_n_Bit_Schieberegister (
  input  ShiftDirection,
  input  Reset,
  input  Enable,
  input  Clock,
  input  Shift,
  input  Set_i_Minus1,
  input  Set_i,
  input  Set_i_Plus1,
  output out_9,
  output out_10,
  output out_11
);

  wire l_2b_d_flipfolp_1_not_q, l_2b_d_flipfolp_2_not_q, l_2b_d_flipfolp_3_not_q, multiplexer_1_out,
       multiplexer_2_out, multiplexer_3_out;

  Multiplexer multiplexer_1 (.in0(Shift), .in1(out_10), .out(multiplexer_1_out), .sel(ShiftDirection));
  Multiplexer multiplexer_2 (.in0(out_9), .in1(out_11), .out(multiplexer_2_out), .sel(ShiftDirection));
  Multiplexer multiplexer_3 (.in0(out_10), .in1(Shift), .out(multiplexer_3_out), .sel(ShiftDirection));
  L_2b_D_Flipfolp l_2b_d_flipfolp_1 (
    .Q(out_9), .NOT_Q(l_2b_d_flipfolp_1_not_q), .Clock(Clock), .Data(multiplexer_1_out), .Enable(Enable),
    .Set(Set_i_Minus1), .Reset(Reset));
  L_2b_D_Flipfolp l_2b_d_flipfolp_2 (
    .Q(out_10), .NOT_Q(l_2b_d_flipfolp_2_not_q), .Clock(Clock), .Data(multiplexer_2_out), .Enable(Enable),
    .Set(Set_i), .Reset(Reset));
  L_2b_D_Flipfolp l_2b_d_flipfolp_3 (
    .Q(out_11), .NOT_Q(l_2b_d_flipfolp_3_not_q), .Clock(Clock), .Data(multiplexer_3_out), .Enable(Enable),
    .Set(Set_i_Plus1), .Reset(Reset));

  // Other names for the same wires on the sheet: Qi = out_10; Qi_Minus1 = out_9; Qi_Plus1 = out_11; Qi_Minus2 = Shift;
  //   Qi_Plus2 = Shift
endmodule

module L_3c_CAS_1bit (
  input  Bin,
  input  Rin,
  input  Tin,
  input  Cin,
  output Tout,
  output Cout,
  output Bout,
  output Rout
);

  wire xor_1_out;

  xor xor_1 (xor_1_out, Tin, Bin);
  L_1b_Adder l_1b_adder_1 (.Si(Rout), .Ci(Cout), .Ai(Rin), .Bi(xor_1_out), .Ci_1(Cin));

  assign Bout = Bin;
  assign Tout = Tin;
endmodule

module L_3c_Divider (
  input  A7,
  input  A6,
  input  A5,
  input  A4,
  input  A3,
  input  A2,
  input  A1,
  input  A0,
  input  B5,
  input  B4,
  input  B3,
  input  B2,
  input  B1,
  input  B0,
  input  A8,
  output Q2,
  output Q1,
  output Q0,
  output R5,
  output R4,
  output R3,
  output R2,
  output R1,
  output R0
);

  wire l_3c_cas_1bit_1_bout, l_3c_cas_1bit_1_rout, l_3c_cas_1bit_1_tout, l_3c_cas_1bit_2_bout,
       l_3c_cas_1bit_2_cout, l_3c_cas_1bit_2_rout, l_3c_cas_1bit_2_tout, l_3c_cas_1bit_3_bout,
       l_3c_cas_1bit_3_rout, l_3c_cas_1bit_3_tout, l_3c_cas_1bit_4_bout, l_3c_cas_1bit_4_cout,
       l_3c_cas_1bit_4_rout, l_3c_cas_1bit_4_tout, l_3c_cas_1bit_5_bout, l_3c_cas_1bit_5_cout,
       l_3c_cas_1bit_5_rout, l_3c_cas_1bit_5_tout, l_3c_cas_1bit_6_bout, l_3c_cas_1bit_6_cout,
       l_3c_cas_1bit_6_rout, l_3c_cas_1bit_6_tout, l_3c_cas_1bit_7_bout, l_3c_cas_1bit_7_cout,
       l_3c_cas_1bit_7_rout, l_3c_cas_1bit_7_tout, l_3c_cas_1bit_8_tout, l_3c_cas_1bit_9_cout,
       l_3c_cas_1bit_9_tout, l_3c_cas_1bit_10_bout, l_3c_cas_1bit_10_cout, l_3c_cas_1bit_10_rout,
       l_3c_cas_1bit_10_tout, l_3c_cas_1bit_11_bout, l_3c_cas_1bit_11_cout, l_3c_cas_1bit_11_rout,
       l_3c_cas_1bit_11_tout, l_3c_cas_1bit_12_cout, l_3c_cas_1bit_12_tout, l_3c_cas_1bit_13_bout,
       l_3c_cas_1bit_13_cout, l_3c_cas_1bit_13_rout, l_3c_cas_1bit_13_tout, l_3c_cas_1bit_14_bout,
       l_3c_cas_1bit_14_cout, l_3c_cas_1bit_14_rout, l_3c_cas_1bit_14_tout, l_3c_cas_1bit_15_cout,
       l_3c_cas_1bit_15_tout, l_3c_cas_1bit_16_bout, l_3c_cas_1bit_16_cout, l_3c_cas_1bit_16_rout,
       l_3c_cas_1bit_16_tout, l_3c_cas_1bit_17_cout, l_3c_cas_1bit_17_tout, l_3c_cas_1bit_18_cout,
       l_3c_cas_1bit_18_tout, xor_1_out;

  xor xor_1 (xor_1_out, B5, ~A8);  // XOR_Gate
  L_3c_CAS_1bit l_3c_cas_1bit_1 (
    .Cout(Q2), .Rout(l_3c_cas_1bit_1_rout), .Tout(l_3c_cas_1bit_1_tout), .Bout(l_3c_cas_1bit_1_bout),
    .Tin(xor_1_out), .Bin(B5), .Rin(A7), .Cin(l_3c_cas_1bit_2_cout));
  L_3c_CAS_1bit l_3c_cas_1bit_2 (
    .Cout(l_3c_cas_1bit_2_cout), .Rout(l_3c_cas_1bit_2_rout), .Tout(l_3c_cas_1bit_2_tout),
    .Bout(l_3c_cas_1bit_2_bout), .Tin(l_3c_cas_1bit_1_tout), .Bin(B4), .Rin(A6), .Cin(l_3c_cas_1bit_4_cout));
  L_3c_CAS_1bit l_3c_cas_1bit_3 (
    .Cout(Q1), .Rout(l_3c_cas_1bit_3_rout), .Tout(l_3c_cas_1bit_3_tout), .Bout(l_3c_cas_1bit_3_bout),
    .Tin(Q2), .Bin(l_3c_cas_1bit_1_bout), .Rin(l_3c_cas_1bit_2_rout), .Cin(l_3c_cas_1bit_6_cout));
  L_3c_CAS_1bit l_3c_cas_1bit_4 (
    .Cout(l_3c_cas_1bit_4_cout), .Rout(l_3c_cas_1bit_4_rout), .Tout(l_3c_cas_1bit_4_tout),
    .Bout(l_3c_cas_1bit_4_bout), .Tin(l_3c_cas_1bit_2_tout), .Bin(B3), .Rin(A5), .Cin(l_3c_cas_1bit_5_cout));
  L_3c_CAS_1bit l_3c_cas_1bit_5 (
    .Cout(l_3c_cas_1bit_5_cout), .Rout(l_3c_cas_1bit_5_rout), .Tout(l_3c_cas_1bit_5_tout),
    .Bout(l_3c_cas_1bit_5_bout), .Tin(l_3c_cas_1bit_4_tout), .Bin(B2), .Rin(A4), .Cin(l_3c_cas_1bit_10_cout));
  L_3c_CAS_1bit l_3c_cas_1bit_6 (
    .Cout(l_3c_cas_1bit_6_cout), .Rout(l_3c_cas_1bit_6_rout), .Tout(l_3c_cas_1bit_6_tout),
    .Bout(l_3c_cas_1bit_6_bout), .Tin(l_3c_cas_1bit_3_tout), .Bin(l_3c_cas_1bit_2_bout),
    .Rin(l_3c_cas_1bit_4_rout), .Cin(l_3c_cas_1bit_7_cout));
  L_3c_CAS_1bit l_3c_cas_1bit_7 (
    .Cout(l_3c_cas_1bit_7_cout), .Rout(l_3c_cas_1bit_7_rout), .Tout(l_3c_cas_1bit_7_tout),
    .Bout(l_3c_cas_1bit_7_bout), .Tin(l_3c_cas_1bit_6_tout), .Bin(l_3c_cas_1bit_4_bout),
    .Rin(l_3c_cas_1bit_5_rout), .Cin(l_3c_cas_1bit_11_cout));
  L_3c_CAS_1bit l_3c_cas_1bit_8 (
    .Cout(Q0), .Rout(R5), .Tout(l_3c_cas_1bit_8_tout), .Tin(Q1), .Bin(l_3c_cas_1bit_3_bout),
    .Rin(l_3c_cas_1bit_6_rout), .Cin(l_3c_cas_1bit_9_cout));  // open: Bout
  L_3c_CAS_1bit l_3c_cas_1bit_9 (
    .Cout(l_3c_cas_1bit_9_cout), .Rout(R4), .Tout(l_3c_cas_1bit_9_tout), .Tin(l_3c_cas_1bit_8_tout),
    .Bin(l_3c_cas_1bit_6_bout), .Rin(l_3c_cas_1bit_7_rout), .Cin(l_3c_cas_1bit_12_cout));  // open: Bout
  L_3c_CAS_1bit l_3c_cas_1bit_10 (
    .Cout(l_3c_cas_1bit_10_cout), .Rout(l_3c_cas_1bit_10_rout), .Tout(l_3c_cas_1bit_10_tout),
    .Bout(l_3c_cas_1bit_10_bout), .Tin(l_3c_cas_1bit_5_tout), .Bin(B1), .Rin(A3), .Cin(l_3c_cas_1bit_13_cout));
  L_3c_CAS_1bit l_3c_cas_1bit_11 (
    .Cout(l_3c_cas_1bit_11_cout), .Rout(l_3c_cas_1bit_11_rout), .Tout(l_3c_cas_1bit_11_tout),
    .Bout(l_3c_cas_1bit_11_bout), .Tin(l_3c_cas_1bit_7_tout), .Bin(l_3c_cas_1bit_5_bout),
    .Rin(l_3c_cas_1bit_10_rout), .Cin(l_3c_cas_1bit_14_cout));
  L_3c_CAS_1bit l_3c_cas_1bit_12 (
    .Cout(l_3c_cas_1bit_12_cout), .Rout(R3), .Tout(l_3c_cas_1bit_12_tout), .Tin(l_3c_cas_1bit_9_tout),
    .Bin(l_3c_cas_1bit_7_bout), .Rin(l_3c_cas_1bit_11_rout), .Cin(l_3c_cas_1bit_15_cout));  // open: Bout
  L_3c_CAS_1bit l_3c_cas_1bit_13 (
    .Cout(l_3c_cas_1bit_13_cout), .Rout(l_3c_cas_1bit_13_rout), .Tout(l_3c_cas_1bit_13_tout),
    .Bout(l_3c_cas_1bit_13_bout), .Tin(l_3c_cas_1bit_10_tout), .Bin(B0), .Rin(A2), .Cin(l_3c_cas_1bit_13_tout));
  L_3c_CAS_1bit l_3c_cas_1bit_14 (
    .Cout(l_3c_cas_1bit_14_cout), .Rout(l_3c_cas_1bit_14_rout), .Tout(l_3c_cas_1bit_14_tout),
    .Bout(l_3c_cas_1bit_14_bout), .Tin(l_3c_cas_1bit_11_tout), .Bin(l_3c_cas_1bit_10_bout),
    .Rin(l_3c_cas_1bit_13_rout), .Cin(l_3c_cas_1bit_16_cout));
  L_3c_CAS_1bit l_3c_cas_1bit_15 (
    .Cout(l_3c_cas_1bit_15_cout), .Rout(R2), .Tout(l_3c_cas_1bit_15_tout), .Tin(l_3c_cas_1bit_12_tout),
    .Bin(l_3c_cas_1bit_11_bout), .Rin(l_3c_cas_1bit_14_rout), .Cin(l_3c_cas_1bit_17_cout));  // open: Bout
  L_3c_CAS_1bit l_3c_cas_1bit_16 (
    .Cout(l_3c_cas_1bit_16_cout), .Rout(l_3c_cas_1bit_16_rout), .Tout(l_3c_cas_1bit_16_tout),
    .Bout(l_3c_cas_1bit_16_bout), .Tin(l_3c_cas_1bit_14_tout), .Bin(l_3c_cas_1bit_13_bout), .Rin(A1),
    .Cin(l_3c_cas_1bit_16_tout));
  L_3c_CAS_1bit l_3c_cas_1bit_17 (
    .Cout(l_3c_cas_1bit_17_cout), .Rout(R1), .Tout(l_3c_cas_1bit_17_tout), .Tin(l_3c_cas_1bit_15_tout),
    .Bin(l_3c_cas_1bit_14_bout), .Rin(l_3c_cas_1bit_16_rout), .Cin(l_3c_cas_1bit_18_cout));  // open: Bout
  L_3c_CAS_1bit l_3c_cas_1bit_18 (
    .Cout(l_3c_cas_1bit_18_cout), .Rout(R0), .Tout(l_3c_cas_1bit_18_tout), .Tin(l_3c_cas_1bit_17_tout),
    .Bin(l_3c_cas_1bit_16_bout), .Rin(A0), .Cin(l_3c_cas_1bit_18_tout));  // open: Bout
endmodule
