// Logisim project Praktikum_Logisim_Woche1.circ as structural Verilog
module _1b__Adder (
  input  Ai,
  input  Bi,
  input  Ci_1,
  output Si,
  output Ci
);

  wire nCi, nSi, transistor_1_out, transistor_2_out, transistor_4_out, transistor_10_out, transistor_11_out,
       transistor_15_out, transistor_18_out, transistor_19_out, transistor_24_out, transistor_26_out;

  Transistor transistor_1 (.in(1'b1), .out(transistor_1_out), .gate(Ai));
  Transistor #(.\type ("n")) transistor_2 (.in(1'b0), .out(transistor_2_out), .gate(Ai));
  Transistor transistor_3 (.in(1'b1), .out(transistor_1_out), .gate(Bi));
  Transistor transistor_4 (.in(transistor_1_out), .out(transistor_4_out), .gate(Ai));
  Transistor transistor_5 (.in(transistor_1_out), .out(nCi), .gate(Ci_1));
  Transistor transistor_6 (.in(transistor_4_out), .out(nCi), .gate(Bi));
  Transistor #(.\type ("n")) transistor_7 (.in(transistor_2_out), .out(nCi), .gate(Ci_1));
  Transistor #(.\type ("n")) transistor_8 (.in(1'b0), .out(transistor_2_out), .gate(Bi));
  Transistor #(.\type ("n")) transistor_9 (.in(transistor_10_out), .out(nCi), .gate(Bi));
  Transistor #(.\type ("n")) transistor_10 (.in(1'b0), .out(transistor_10_out), .gate(Ai));
  Transistor transistor_11 (.in(1'b1), .out(transistor_11_out), .gate(Ai));
  Transistor transistor_12 (.in(1'b1), .out(transistor_11_out), .gate(Bi));
  Transistor transistor_13 (.in(transistor_11_out), .out(nSi), .gate(nCi));
  Transistor #(.\type ("n")) transistor_14 (.in(transistor_15_out), .out(nSi), .gate(nCi));
  Transistor #(.\type ("n")) transistor_15 (.in(1'b0), .out(transistor_15_out), .gate(Bi));
  Transistor #(.\type ("n")) transistor_16 (.in(1'b0), .out(transistor_15_out), .gate(Ai));
  Transistor transistor_17 (.in(1'b1), .out(transistor_11_out), .gate(Ci_1));
  Transistor transistor_18 (.in(transistor_11_out), .out(transistor_18_out), .gate(Ci_1));
  Transistor transistor_19 (.in(transistor_18_out), .out(transistor_19_out), .gate(Bi));
  Transistor transistor_20 (.in(transistor_19_out), .out(nSi), .gate(Ai));
  Transistor #(.\type ("n")) transistor_21 (.in(1'b0), .out(transistor_15_out), .gate(Ci_1));
  Transistor transistor_22 (.in(1'b1), .out(Ci), .gate(nCi));
  Transistor #(.\type ("n")) transistor_23 (.in(transistor_24_out), .out(nSi), .gate(Ci_1));
  Transistor #(.\type ("n")) transistor_24 (.in(transistor_26_out), .out(transistor_24_out), .gate(Bi));
  Transistor #(.\type ("n")) transistor_25 (.in(1'b0), .out(Ci), .gate(nCi));
  Transistor #(.\type ("n")) transistor_26 (.in(1'b0), .out(transistor_26_out), .gate(Ai));
  Transistor transistor_27 (.in(1'b1), .out(Si), .gate(nSi));
  Transistor #(.\type ("n")) transistor_28 (.in(1'b0), .out(Si), .gate(nSi));
endmodule

module _1c__Transmission_Gates (
  input  y,
  input  x,
  output f_x_y
);

  wire and_1_out, not_2_out, not_3_out, or_1_out, or_2_out, transistor_1_out, transistor_3_out,
       transistor_4_out, transistor_7_out, transistor_8_out, transistor_11_out, transistor_12_out,
       transistor_15_out, transistor_17_out, transistor_21_out, transistor_22_out, transistor_24_out,
       transistor_25_out, transistor_28_out, transistor_29_out, transistor_30_out, transistor_32_out,
       transistor_33_out, transistor_36_out, transistor_37_out, transistor_40_out, transistor_41_out,
       transistor_45_out, transistor_47_out, transistor_48_out, transistor_51_out, transistor_52_out,
       transistor_54_out, transistor_55_out, transmission_1_p1, transmission_1_p3;

  Transistor transistor_1 (.in(1'b1), .out(transistor_1_out), .gate(y));
  Transistor #(.\type ("n")) transistor_2 (.in(1'b0), .out(transistor_1_out), .gate(y));
  // Transmission_Gate transmission_1: pin names not known; wires that end beside it: transmission_1_p1, y, transmission_1_p3
  not not_1 (transmission_1_p1, x);
  not not_2 (not_2_out, y);
  // Transmission_Gate transmission_2: pin names not known; wires that end beside it: x, not_2_out, y, transmission_1_p3, transmission_1_p3
  Transistor transistor_3 (.in(1'b1), .out(transistor_3_out), .gate(x));
  Transistor transistor_4 (.in(1'b1), .out(transistor_4_out), .gate(y));
  Transistor #(.\type ("n")) transistor_5 (.in(1'b0), .out(transistor_4_out), .gate(y));
  Transistor #(.\type ("n")) transistor_6 (.in(1'b0), .out(transistor_3_out), .gate(x));
  Transistor transistor_7 (.in(1'b1), .out(transistor_7_out), .gate(x));
  Transistor transistor_8 (.in(1'b1), .out(transistor_8_out), .gate(y));
  Transistor #(.\type ("n")) transistor_9 (.in(1'b0), .out(transistor_8_out), .gate(y));
  Transistor #(.\type ("n")) transistor_10 (.in(1'b0), .out(transistor_7_out), .gate(x));
  Transistor transistor_11 (.in(1'b1), .out(transistor_11_out), .gate(x));
  Transistor transistor_12 (.in(1'b1), .out(transistor_12_out), .gate(y));
  Transistor #(.\type ("n")) transistor_13 (.in(1'b0), .out(transistor_12_out), .gate(y));
  Transistor #(.\type ("n")) transistor_14 (.in(1'b0), .out(transistor_11_out), .gate(x));
  Transistor transistor_15 (.in(1'b1), .out(transistor_15_out), .gate(x));
  Transistor #(.\type ("n")) transistor_16 (.in(1'b0), .out(transistor_15_out), .gate(x));
  Transistor transistor_17 (.in(transistor_3_out), .out(transistor_17_out), .gate(y));
  Transistor #(.\type ("n"), .gate("br")) transistor_18 (
    .in(transistor_3_out), .out(transistor_17_out), .gate(transistor_4_out));
  Transistor transistor_19 (.in(x), .out(transistor_17_out), .gate(transistor_4_out));
  Transistor #(.\type ("n"), .gate("br")) transistor_20 (.in(x), .out(transistor_17_out), .gate(y));
  Transistor transistor_21 (.in(1'b1), .out(transistor_21_out), .gate(y));
  Transistor transistor_22 (.in(transistor_21_out), .out(transistor_22_out), .gate(transistor_7_out));
  Transistor #(.\type ("n")) transistor_23 (.in(transistor_24_out), .out(transistor_22_out), .gate(y));
  Transistor #(.\type ("n")) transistor_24 (.in(1'b0), .out(transistor_24_out), .gate(x));
  Transistor transistor_25 (.in(1'b1), .out(transistor_25_out), .gate(x));
  Transistor transistor_26 (.in(transistor_25_out), .out(f_x_y), .gate(y));
  Transistor #(.\type ("n")) transistor_27 (.in(transistor_28_out), .out(f_x_y), .gate(transistor_11_out));
  Transistor #(.\type ("n")) transistor_28 (.in(1'b0), .out(transistor_28_out), .gate(y));
  Transistor transistor_29 (.in(1'b1), .out(transistor_29_out), .gate(y));
  Transistor transistor_30 (.in(transistor_29_out), .out(transistor_30_out), .gate(x));
  Transistor #(.\type ("n")) transistor_31 (.in(transistor_32_out), .out(transistor_30_out), .gate(y));
  Transistor #(.\type ("n")) transistor_32 (.in(1'b0), .out(transistor_32_out), .gate(transistor_15_out));
  Transistor transistor_33 (.in(1'b1), .out(transistor_33_out), .gate(transistor_8_out));
  Transistor transistor_34 (.in(transistor_33_out), .out(transistor_22_out), .gate(x));
  Transistor #(.\type ("n")) transistor_35 (.in(transistor_36_out), .out(transistor_22_out), .gate(transistor_8_out));
  Transistor #(.\type ("n")) transistor_36 (.in(1'b0), .out(transistor_36_out), .gate(transistor_7_out));
  Transistor transistor_37 (.in(1'b1), .out(transistor_37_out), .gate(transistor_12_out));
  Transistor transistor_38 (.in(transistor_37_out), .out(f_x_y), .gate(transistor_11_out));
  Transistor #(.\type ("n")) transistor_39 (.in(transistor_40_out), .out(f_x_y), .gate(x));
  Transistor #(.\type ("n")) transistor_40 (.in(1'b0), .out(transistor_40_out), .gate(transistor_12_out));
  Transistor transistor_41 (.in(1'b1), .out(transistor_41_out), .gate(transistor_1_out));
  Transistor transistor_42 (.in(transistor_41_out), .out(transistor_30_out), .gate(transistor_15_out));
  Transistor #(.\type ("n")) transistor_43 (.in(transistor_32_out), .out(transistor_30_out), .gate(x));
  Transistor #(.\type ("n")) transistor_44 (.in(1'b0), .out(transistor_32_out), .gate(transistor_1_out));
  Transistor transistor_45 (.in(1'b1), .out(transistor_45_out), .gate(transistor_22_out));
  Transistor #(.\type ("n")) transistor_46 (.in(1'b0), .out(transistor_45_out), .gate(transistor_22_out));
  and and_1 (and_1_out, y, x);
  not not_3 (not_3_out, or_1_out);
  or or_1 (or_1_out, x, y);
  Transistor transistor_47 (.in(1'b1), .out(transistor_47_out), .gate(y));
  Transistor transistor_48 (.in(1'b1), .out(transistor_48_out), .gate(x));
  Transistor #(.\type ("n")) transistor_49 (.in(1'b0), .out(transistor_47_out), .gate(y));
  Transistor #(.\type ("n")) transistor_50 (.in(1'b0), .out(transistor_48_out), .gate(x));
  or or_2 (or_2_out, and_1_out, not_3_out);
  Transistor transistor_51 (.in(1'b1), .out(transistor_51_out), .gate(x));
  Transistor transistor_52 (.in(transistor_51_out), .out(transistor_52_out), .gate(y));
  Transistor #(.\type ("n")) transistor_53 (.in(transistor_54_out), .out(transistor_52_out), .gate(y));
  Transistor #(.\type ("n")) transistor_54 (.in(1'b0), .out(transistor_54_out), .gate(transistor_48_out));
  // XNOR_Gate xnor_1 is placed but not wired
  Transistor transistor_55 (.in(1'b1), .out(transistor_55_out), .gate(transistor_48_out));
  Transistor transistor_56 (.in(transistor_55_out), .out(transistor_52_out), .gate(transistor_47_out));
  Transistor #(.\type ("n")) transistor_57 (.in(transistor_54_out), .out(transistor_52_out), .gate(x));
  Transistor #(.\type ("n")) transistor_58 (.in(1'b0), .out(transistor_54_out), .gate(transistor_47_out));

  // Notes on the sheet:
  //   Angabe
  //   Angabe nur mit Transistoren
  //   CMOS-XOR aus Vorlesung => XOR
  //   Identisch, aber basierend auf Gleichheits-Formel, nach CMOS vorgehen
  //   CMOS-XOR aus Vorlesung + Inverter => XNOR
  //   ABER: PUN und PDN Vertauscht! => XNOR
  //   I) Schaltdiagramm implementiert (y*!x)+(!y*x)
  //   => Gleichheit
  //   II) 8 Transistoren
  //   III) 12 Transistoren
  //   XNOR/Equals
endmodule

module _1d__n_Bit_CAS (
  input  Add,
  input  a1,
  input  b1,
  input  a2,
  input  b2,
  input  a3,
  input  b3,
  input  a4,
  input  b4,
  input  a5,
  input  b5,
  input  a6,
  input  b6,
  input  a7,
  input  b7,
  input  a8,
  input  b8,
  output s1,
  output s2,
  output s3,
  output s4,
  output s5,
  output s6,
  output s7,
  output s8
);

  wire n1b_adder_1_ci, n1b_adder_2_ci, n1b_adder_3_ci, n1b_adder_4_ci, n1b_adder_5_ci, n1b_adder_6_ci,
       n1b_adder_7_ci, n1b_adder_8_ci, n1c_transmissions_1_f_x_y, n1c_transmissions_2_f_x_y,
       n1c_transmissions_3_f_x_y, n1c_transmissions_4_f_x_y, n1c_transmissions_5_f_x_y,
       n1c_transmissions_6_f_x_y, n1c_transmissions_7_f_x_y, n1c_transmissions_8_f_x_y,
       n1c_transmissions_9_f_x_y;

  _1c__Transmission_Gates u_1c_transmissions_1 (.f_x_y(n1c_transmissions_1_f_x_y), .y(1'b0), .x(Add));
  _1c__Transmission_Gates u_1c_transmissions_2 (.f_x_y(n1c_transmissions_2_f_x_y), .y(Add), .x(b1));
  _1c__Transmission_Gates u_1c_transmissions_3 (.f_x_y(n1c_transmissions_3_f_x_y), .y(Add), .x(b2));
  _1c__Transmission_Gates u_1c_transmissions_4 (.f_x_y(n1c_transmissions_4_f_x_y), .y(Add), .x(b3));
  _1c__Transmission_Gates u_1c_transmissions_5 (.f_x_y(n1c_transmissions_5_f_x_y), .y(Add), .x(b4));
  _1c__Transmission_Gates u_1c_transmissions_6 (.f_x_y(n1c_transmissions_6_f_x_y), .y(Add), .x(b5));
  _1c__Transmission_Gates u_1c_transmissions_7 (.f_x_y(n1c_transmissions_7_f_x_y), .y(Add), .x(b6));
  _1c__Transmission_Gates u_1c_transmissions_8 (.f_x_y(n1c_transmissions_8_f_x_y), .y(Add), .x(b7));
  _1c__Transmission_Gates u_1c_transmissions_9 (.f_x_y(n1c_transmissions_9_f_x_y), .y(Add), .x(b8));
  _1b__Adder u_1b_adder_1 (
    .Ai(a1), .Bi(n1c_transmissions_2_f_x_y), .Ci_1(n1c_transmissions_1_f_x_y), .Si(s1), .Ci(n1b_adder_1_ci));
  _1b__Adder u_1b_adder_2 (
    .Ai(a2), .Bi(n1c_transmissions_3_f_x_y), .Ci_1(n1b_adder_1_ci), .Si(s2), .Ci(n1b_adder_2_ci));
  _1b__Adder u_1b_adder_3 (
    .Ai(a3), .Bi(n1c_transmissions_4_f_x_y), .Ci_1(n1b_adder_2_ci), .Si(s3), .Ci(n1b_adder_3_ci));
  _1b__Adder u_1b_adder_4 (
    .Ai(a4), .Bi(n1c_transmissions_5_f_x_y), .Ci_1(n1b_adder_3_ci), .Si(s4), .Ci(n1b_adder_4_ci));
  _1b__Adder u_1b_adder_5 (
    .Ai(a5), .Bi(n1c_transmissions_6_f_x_y), .Ci_1(n1b_adder_4_ci), .Si(s5), .Ci(n1b_adder_5_ci));
  _1b__Adder u_1b_adder_6 (
    .Ai(a6), .Bi(n1c_transmissions_7_f_x_y), .Ci_1(n1b_adder_5_ci), .Si(s6), .Ci(n1b_adder_6_ci));
  _1b__Adder u_1b_adder_7 (
    .Ai(a7), .Bi(n1c_transmissions_8_f_x_y), .Ci_1(n1b_adder_6_ci), .Si(s7), .Ci(n1b_adder_7_ci));
  _1b__Adder u_1b_adder_8 (
    .Ai(a8), .Bi(n1c_transmissions_9_f_x_y), .Ci_1(n1b_adder_7_ci), .Si(s8), .Ci(n1b_adder_8_ci));
endmodule

module _2a__Wellenform_Diagramm (
  input  R,
  input  S,
  output Q,
  output nQ
);

  nor nor_1 (Q, R, nQ);
  nor nor_2 (nQ, Q, S);

  // Notes on the sheet:
  //   R
  //   S
  //   Q
  //   !Q
  //   0
  //   20
  //   60
  //   80
  //   40
  //   160
  //   140
  //   120
  //   100
  //   240
  //   220
  //   200
  //   180
  //   t[ns]
  //   260
  //   280
endmodule

module _2b__D_Flipfolp (
  input  Data,
  input  Enable,
  input  Clock,
  input  Set,
  input  Reset,
  output Q,
  output nQ
);

  wire and_1_out, and_2_out, and_3_out, buffer_1_out, buffer_2_out, nor_1_out, not_1_out, not_2_out,
       or_1_out, or_2_out;

  buf buffer_1 (buffer_1_out, Clock);
  not not_1 (not_1_out, buffer_1_out);
  not not_2 (not_2_out, Data);
  buf buffer_2 (buffer_2_out, Data);
  and and_1 (and_1_out, Enable, nor_1_out);
  nor nor_1 (nor_1_out, not_1_out, Clock);
  and and_2 (and_2_out, not_2_out, and_1_out);
  and and_3 (and_3_out, buffer_2_out, and_1_out);
  or or_1 (or_1_out, and_2_out, Reset);
  or or_2 (or_2_out, and_3_out, Set);
  _2a__Wellenform_Diagramm u_2a_wellenform_diagramm_1 (.R(or_1_out), .S(or_2_out), .Q(Q), .nQ(nQ));
endmodule

module _2c__n_Bit_Register (
  input  Reset,
  input  Set,
  input  Enable,
  input  CLK,
  input  Data1,
  input  Data2,
  input  Data3,
  input  Data4,
  input  Data5,
  input  Data6,
  input  Data7,
  input  Data8,
  output Out1,
  output Out2,
  output Out3,
  output Out4,
  output Out5,
  output Out6,
  output Out7,
  output Out8
);

  wire n2b_d_flipfolp_1_nq, n2b_d_flipfolp_2_nq, n2b_d_flipfolp_3_nq, n2b_d_flipfolp_4_nq,
       n2b_d_flipfolp_5_nq, n2b_d_flipfolp_6_nq, n2b_d_flipfolp_7_nq, n2b_d_flipfolp_8_nq;

  _2b__D_Flipfolp u_2b_d_flipfolp_1 (
    .Data(Data1), .Q(Out1), .nQ(n2b_d_flipfolp_1_nq), .Enable(Enable), .Clock(CLK), .Set(Set), .Reset(Reset));
  _2b__D_Flipfolp u_2b_d_flipfolp_2 (
    .Data(Data2), .Q(Out2), .nQ(n2b_d_flipfolp_2_nq), .Enable(Enable), .Clock(CLK), .Set(Set), .Reset(Reset));
  _2b__D_Flipfolp u_2b_d_flipfolp_3 (
    .Data(Data3), .Q(Out3), .nQ(n2b_d_flipfolp_3_nq), .Enable(Enable), .Clock(CLK), .Set(Set), .Reset(Reset));
  _2b__D_Flipfolp u_2b_d_flipfolp_4 (
    .Data(Data4), .Q(Out4), .nQ(n2b_d_flipfolp_4_nq), .Enable(Enable), .Clock(CLK), .Set(Set), .Reset(Reset));
  _2b__D_Flipfolp u_2b_d_flipfolp_5 (
    .Data(Data5), .Q(Out5), .nQ(n2b_d_flipfolp_5_nq), .Enable(Enable), .Clock(CLK), .Set(Set), .Reset(Reset));
  _2b__D_Flipfolp u_2b_d_flipfolp_6 (
    .Data(Data6), .Q(Out6), .nQ(n2b_d_flipfolp_6_nq), .Enable(Enable), .Clock(CLK), .Set(Set), .Reset(Reset));
  _2b__D_Flipfolp u_2b_d_flipfolp_7 (
    .Data(Data7), .Q(Out7), .nQ(n2b_d_flipfolp_7_nq), .Enable(Enable), .Clock(CLK), .Set(Set), .Reset(Reset));
  _2b__D_Flipfolp u_2b_d_flipfolp_8 (
    .Data(Data8), .Q(Out8), .nQ(n2b_d_flipfolp_8_nq), .Enable(Enable), .Clock(CLK), .Set(Set), .Reset(Reset));
endmodule

module _2c__n_Bit_Schieberegister (
  input  ShiftDirection,
  input  Reset,
  input  Enable,
  input  Clock,
  input  Shift,
  input  Set_i_1,
  input  Set_i,
  input  Set_i_1_2,
  output out_9,
  output out_10,
  output out_11
);

  wire multiplexer_1_out, multiplexer_2_out, multiplexer_3_out, n2b_d_flipfolp_1_nq, n2b_d_flipfolp_2_nq,
       n2b_d_flipfolp_3_nq;

  Multiplexer #(.disabled(0), .enable("false")) multiplexer_1 (
    .in0(Shift), .in1(out_10), .out(multiplexer_1_out), .sel(ShiftDirection));
  Multiplexer #(.disabled(0), .enable("false")) multiplexer_2 (
    .in0(out_9), .in1(out_11), .out(multiplexer_2_out), .sel(ShiftDirection));
  Multiplexer #(.disabled(0), .enable("false")) multiplexer_3 (
    .in0(out_10), .in1(Shift), .out(multiplexer_3_out), .sel(ShiftDirection));
  _2b__D_Flipfolp u_2b_d_flipfolp_1 (
    .Data(multiplexer_1_out), .Q(out_9), .nQ(n2b_d_flipfolp_1_nq), .Enable(Enable), .Clock(Clock),
    .Set(Set_i_1), .Reset(Reset));
  _2b__D_Flipfolp u_2b_d_flipfolp_2 (
    .Data(multiplexer_2_out), .Q(out_10), .nQ(n2b_d_flipfolp_2_nq), .Enable(Enable), .Clock(Clock),
    .Set(Set_i), .Reset(Reset));
  _2b__D_Flipfolp u_2b_d_flipfolp_3 (
    .Data(multiplexer_3_out), .Q(out_11), .nQ(n2b_d_flipfolp_3_nq), .Enable(Enable), .Clock(Clock),
    .Set(Set_i_1_2), .Reset(Reset));

  // Other names for the same wires on the sheet: Qi = out_10; Qi_1 = out_11; Qi_1_t = out_9; Qi_2 = Shift
endmodule

module _3c__CAS__1bit (
  input  Bin,
  input  Rin,
  input  Tin,
  input  Cin,
  output Tout,
  output Cout,
  output Bout,
  output Rout
);

  wire xor_1_out;

  xor xor_1 (xor_1_out, Tin, Bin);
  _1b__Adder u_1b_adder_1 (.Ai(Rin), .Bi(xor_1_out), .Ci_1(Cin), .Si(Rout), .Ci(Cout));

  assign Bout = Bin;
  assign Tout = Tin;
endmodule

module _3c__Divider (
  input  A7,
  input  A6,
  input  A5,
  input  A4,
  input  A3,
  input  A2,
  input  A1,
  input  A0,
  input  B5,
  input  B4,
  input  B3,
  input  B2,
  input  B1,
  input  B0,
  input  A8,
  output Q2,
  output Q1,
  output Q0,
  output R5,
  output R4,
  output R3,
  output R2,
  output R1,
  output R0
);

  wire n3c_cas_1bit_1_bout, n3c_cas_1bit_1_rout, n3c_cas_1bit_1_tout, n3c_cas_1bit_2_bout,
       n3c_cas_1bit_2_cout, n3c_cas_1bit_2_rout, n3c_cas_1bit_2_tout, n3c_cas_1bit_3_bout,
       n3c_cas_1bit_3_rout, n3c_cas_1bit_3_tout, n3c_cas_1bit_4_bout, n3c_cas_1bit_4_cout,
       n3c_cas_1bit_4_rout, n3c_cas_1bit_4_tout, n3c_cas_1bit_5_bout, n3c_cas_1bit_5_cout,
       n3c_cas_1bit_5_rout, n3c_cas_1bit_5_tout, n3c_cas_1bit_6_bout, n3c_cas_1bit_6_cout,
       n3c_cas_1bit_6_rout, n3c_cas_1bit_6_tout, n3c_cas_1bit_7_bout, n3c_cas_1bit_7_cout,
       n3c_cas_1bit_7_rout, n3c_cas_1bit_7_tout, n3c_cas_1bit_8_cout, n3c_cas_1bit_8_tout,
       n3c_cas_1bit_9_tout, n3c_cas_1bit_10_bout, n3c_cas_1bit_10_cout, n3c_cas_1bit_10_rout,
       n3c_cas_1bit_10_tout, n3c_cas_1bit_11_bout, n3c_cas_1bit_11_cout, n3c_cas_1bit_11_rout,
       n3c_cas_1bit_11_tout, n3c_cas_1bit_12_cout, n3c_cas_1bit_12_tout, n3c_cas_1bit_13_bout,
       n3c_cas_1bit_13_cout, n3c_cas_1bit_13_rout, n3c_cas_1bit_13_tout, n3c_cas_1bit_14_bout,
       n3c_cas_1bit_14_cout, n3c_cas_1bit_14_rout, n3c_cas_1bit_14_tout, n3c_cas_1bit_15_cout,
       n3c_cas_1bit_15_tout, n3c_cas_1bit_16_bout, n3c_cas_1bit_16_cout, n3c_cas_1bit_16_rout,
       n3c_cas_1bit_16_tout, n3c_cas_1bit_17_cout, n3c_cas_1bit_17_tout, n3c_cas_1bit_18_cout,
       n3c_cas_1bit_18_tout, xor_1_out;

  xor xor_1 (xor_1_out, B5, ~A8);  // XOR_Gate
  _3c__CAS__1bit u_3c_cas_1bit_1 (
    .Bin(B5), .Rin(A7), .Tin(xor_1_out), .Cin(n3c_cas_1bit_2_cout), .Cout(Q2), .Bout(n3c_cas_1bit_1_bout),
    .Rout(n3c_cas_1bit_1_rout), .Tout(n3c_cas_1bit_1_tout));
  _3c__CAS__1bit u_3c_cas_1bit_2 (
    .Bin(B4), .Rin(A6), .Tin(n3c_cas_1bit_1_tout), .Cin(n3c_cas_1bit_4_cout), .Cout(n3c_cas_1bit_2_cout),
    .Bout(n3c_cas_1bit_2_bout), .Rout(n3c_cas_1bit_2_rout), .Tout(n3c_cas_1bit_2_tout));
  _3c__CAS__1bit u_3c_cas_1bit_3 (
    .Bin(n3c_cas_1bit_1_bout), .Rin(n3c_cas_1bit_2_rout), .Tin(Q2), .Cin(n3c_cas_1bit_6_cout), .Cout(Q1),
    .Bout(n3c_cas_1bit_3_bout), .Rout(n3c_cas_1bit_3_rout), .Tout(n3c_cas_1bit_3_tout));
  _3c__CAS__1bit u_3c_cas_1bit_4 (
    .Bin(B3), .Rin(A5), .Tin(n3c_cas_1bit_2_tout), .Cin(n3c_cas_1bit_5_cout), .Cout(n3c_cas_1bit_4_cout),
    .Bout(n3c_cas_1bit_4_bout), .Rout(n3c_cas_1bit_4_rout), .Tout(n3c_cas_1bit_4_tout));
  _3c__CAS__1bit u_3c_cas_1bit_5 (
    .Bin(B2), .Rin(A4), .Tin(n3c_cas_1bit_4_tout), .Cin(n3c_cas_1bit_10_cout), .Cout(n3c_cas_1bit_5_cout),
    .Bout(n3c_cas_1bit_5_bout), .Rout(n3c_cas_1bit_5_rout), .Tout(n3c_cas_1bit_5_tout));
  _3c__CAS__1bit u_3c_cas_1bit_6 (
    .Bin(n3c_cas_1bit_2_bout), .Rin(n3c_cas_1bit_4_rout), .Tin(n3c_cas_1bit_3_tout),
    .Cin(n3c_cas_1bit_7_cout), .Cout(n3c_cas_1bit_6_cout), .Bout(n3c_cas_1bit_6_bout),
    .Rout(n3c_cas_1bit_6_rout), .Tout(n3c_cas_1bit_6_tout));
  _3c__CAS__1bit u_3c_cas_1bit_7 (
    .Bin(n3c_cas_1bit_4_bout), .Rin(n3c_cas_1bit_5_rout), .Tin(n3c_cas_1bit_6_tout),
    .Cin(n3c_cas_1bit_11_cout), .Cout(n3c_cas_1bit_7_cout), .Bout(n3c_cas_1bit_7_bout),
    .Rout(n3c_cas_1bit_7_rout), .Tout(n3c_cas_1bit_7_tout));
  _3c__CAS__1bit u_3c_cas_1bit_8 (
    .Bin(n3c_cas_1bit_6_bout), .Rin(n3c_cas_1bit_7_rout), .Tin(n3c_cas_1bit_9_tout),
    .Cin(n3c_cas_1bit_12_cout), .Cout(n3c_cas_1bit_8_cout), .Rout(R4), .Tout(n3c_cas_1bit_8_tout));  // open: Bout
  _3c__CAS__1bit u_3c_cas_1bit_9 (
    .Bin(n3c_cas_1bit_3_bout), .Rin(n3c_cas_1bit_6_rout), .Tin(Q1), .Cin(n3c_cas_1bit_8_cout), .Cout(Q0),
    .Rout(R5), .Tout(n3c_cas_1bit_9_tout));  // open: Bout
  _3c__CAS__1bit u_3c_cas_1bit_10 (
    .Bin(B1), .Rin(A3), .Tin(n3c_cas_1bit_5_tout), .Cin(n3c_cas_1bit_13_cout), .Cout(n3c_cas_1bit_10_cout),
    .Bout(n3c_cas_1bit_10_bout), .Rout(n3c_cas_1bit_10_rout), .Tout(n3c_cas_1bit_10_tout));
  _3c__CAS__1bit u_3c_cas_1bit_11 (
    .Bin(n3c_cas_1bit_5_bout), .Rin(n3c_cas_1bit_10_rout), .Tin(n3c_cas_1bit_7_tout),
    .Cin(n3c_cas_1bit_14_cout), .Cout(n3c_cas_1bit_11_cout), .Bout(n3c_cas_1bit_11_bout),
    .Rout(n3c_cas_1bit_11_rout), .Tout(n3c_cas_1bit_11_tout));
  _3c__CAS__1bit u_3c_cas_1bit_12 (
    .Bin(n3c_cas_1bit_7_bout), .Rin(n3c_cas_1bit_11_rout), .Tin(n3c_cas_1bit_8_tout),
    .Cin(n3c_cas_1bit_15_cout), .Cout(n3c_cas_1bit_12_cout), .Rout(R3), .Tout(n3c_cas_1bit_12_tout));  // open: Bout
  _3c__CAS__1bit u_3c_cas_1bit_13 (
    .Bin(B0), .Rin(A2), .Tin(n3c_cas_1bit_10_tout), .Cin(n3c_cas_1bit_13_tout), .Cout(n3c_cas_1bit_13_cout),
    .Bout(n3c_cas_1bit_13_bout), .Rout(n3c_cas_1bit_13_rout), .Tout(n3c_cas_1bit_13_tout));
  _3c__CAS__1bit u_3c_cas_1bit_14 (
    .Bin(n3c_cas_1bit_10_bout), .Rin(n3c_cas_1bit_13_rout), .Tin(n3c_cas_1bit_11_tout),
    .Cin(n3c_cas_1bit_16_cout), .Cout(n3c_cas_1bit_14_cout), .Bout(n3c_cas_1bit_14_bout),
    .Rout(n3c_cas_1bit_14_rout), .Tout(n3c_cas_1bit_14_tout));
  _3c__CAS__1bit u_3c_cas_1bit_15 (
    .Bin(n3c_cas_1bit_11_bout), .Rin(n3c_cas_1bit_14_rout), .Tin(n3c_cas_1bit_12_tout),
    .Cin(n3c_cas_1bit_17_cout), .Cout(n3c_cas_1bit_15_cout), .Rout(R2), .Tout(n3c_cas_1bit_15_tout));  // open: Bout
  _3c__CAS__1bit u_3c_cas_1bit_16 (
    .Bin(n3c_cas_1bit_13_bout), .Rin(A1), .Tin(n3c_cas_1bit_14_tout), .Cin(n3c_cas_1bit_16_tout),
    .Cout(n3c_cas_1bit_16_cout), .Bout(n3c_cas_1bit_16_bout), .Rout(n3c_cas_1bit_16_rout),
    .Tout(n3c_cas_1bit_16_tout));
  _3c__CAS__1bit u_3c_cas_1bit_17 (
    .Bin(n3c_cas_1bit_14_bout), .Rin(n3c_cas_1bit_16_rout), .Tin(n3c_cas_1bit_15_tout),
    .Cin(n3c_cas_1bit_18_cout), .Cout(n3c_cas_1bit_17_cout), .Rout(R1), .Tout(n3c_cas_1bit_17_tout));  // open: Bout
  _3c__CAS__1bit u_3c_cas_1bit_18 (
    .Bin(n3c_cas_1bit_16_bout), .Rin(A0), .Tin(n3c_cas_1bit_17_tout), .Cin(n3c_cas_1bit_18_tout),
    .Cout(n3c_cas_1bit_18_cout), .Rout(R0), .Tout(n3c_cas_1bit_18_tout));  // open: Bout
endmodule
