// Logisim project RS_Latches.circ as structural Verilog: 3 circuits, main circuit LatchVergleich
module LatchVergleich (
);

  wire nand_rs_latch_1_not_q, nand_rs_latch_1_q, nor_rs_latch_1_not_q, nor_rs_latch_1_q;

  NOR_RS_Latch nor_rs_latch_1 (
    .Set(1'b1), .Clock(1'b1), .Reset(1'b1), .NOT_Q(nor_rs_latch_1_not_q), .Q(nor_rs_latch_1_q));
  NAND_RS_Latch nand_rs_latch_1 (
    .Set(1'b1), .Clock(1'b1), .Reset(1'b1), .Q(nand_rs_latch_1_q), .NOT_Q(nand_rs_latch_1_not_q));

  // Notes on the sheet:
  //   Unterschied zwischen NAND- und NOR-RS-Latches:
  //   NOR-RS-Latch ist im Illegalen Zustand LOW:
  //   NAND-RS-Latch ist im illegalen Zustand HIGH:
endmodule

module NOR_RS_Latch (
  input  Set,
  input  Clock,
  input  Reset,
  output NOT_Q,
  output Q
);

  wire and_1_out, and_2_out;

  and and_1 (and_1_out, Set, Clock);
  and and_2 (and_2_out, Clock, Reset);
  nor nor_1 (NOT_Q, and_1_out, Q);
  nor nor_2 (Q, NOT_Q, and_2_out);
endmodule

module NAND_RS_Latch (
  input  Set,
  input  Clock,
  input  Reset,
  output Q,
  output NOT_Q
);

  wire nand_1_out, nand_2_out;

  nand nand_1 (nand_1_out, Set, Clock);
  nand nand_2 (nand_2_out, Clock, Reset);
  nand nand_3 (Q, nand_1_out, NOT_Q);
  nand nand_4 (NOT_Q, Q, nand_2_out);
endmodule
