// Logisim project 2d_Schaltwerk.circ as structural Verilog: 1 circuit, main circuit main
module main (
  input  Enable,
  input  BTN_0,
  input  BTN_1
);

  wire and_1_out, and_2_out, and_3_out, and_4_out, and_5_out, and_6_out, CLK_out, d_ff_1_q, or_1_out,
       or_2_out, q0_q;

  and and_1 (and_1_out, ~q0_q, BTN_0, ~BTN_1);  // AND_Gate
  and and_2 (and_2_out, q0_q, ~BTN_0, ~BTN_1);  // AND_Gate
  and and_3 (and_3_out, q0_q, BTN_0, BTN_1);
  and and_4 (and_4_out, ~d_ff_1_q, ~BTN_0, BTN_1);  // AND_Gate
  and and_5 (and_5_out, d_ff_1_q, ~BTN_0, ~BTN_1);  // AND_Gate
  and and_6 (and_6_out, d_ff_1_q, BTN_0, BTN_1);
  or or_1 (or_1_out, and_1_out, and_2_out, and_3_out);
  or or_2 (or_2_out, and_4_out, and_5_out, and_6_out);
  Clock CLK (.out(CLK_out));
  D_Flip_Flop q0 (.clk(CLK_out), .D(or_1_out), .Q(q0_q), .en(Enable));  // open: Qn, preset, reset
  D_Flip_Flop d_ff_1 (.clk(CLK_out), .D(or_2_out), .Q(d_ff_1_q), .en(Enable));  // open: Qn, preset, reset
endmodule
