// Logisim project Praktikum_Logisim_Woche2.circ as structural Verilog: 6 circuits, main circuit 1a_Funktion
module _1a_Funktion (
  input  CLK,
  input  BTN2,
  output E0_Falling_Edge_Detection,
  output E1_Rising_Edge_Detection,
  output E2_Button_Pressed,
  output E3_Button_Released,
  output NOT_NOT_BTN2,
  output NOT_BTN2
);

  wire not_3_out;

  nor G2 (E2_Button_Pressed, NOT_NOT_BTN2, NOT_BTN2);
  nor G4 (E0_Falling_Edge_Detection, not_3_out, CLK);
  and G3 (E1_Rising_Edge_Detection, not_3_out, CLK);
  and G1 (E3_Button_Released, NOT_BTN2, NOT_NOT_BTN2);
  not not_1 (NOT_BTN2, BTN2);
  not not_2 (NOT_NOT_BTN2, NOT_BTN2);
  not not_3 (not_3_out, CLK);
endmodule

module _1b_Wellenformdiagramm (
);


  // Notes on the sheet:
  //   BTN₂
  //   G₁
  //   G₂
  //   CLK
  //   G₃
  //   G₄
endmodule

module _1c_NOR (
  input  S,
  input  C,
  input  R,
  output NOT_Q,
  output Q
);

  wire and_1_out, and_2_out;

  nor nor_1 (NOT_Q, and_1_out, Q);
  nor nor_2 (Q, NOT_Q, and_2_out);
  and and_1 (and_1_out, S, C);
  and and_2 (and_2_out, C, R);
endmodule

module _1c_NAND (
  input  S,
  input  C,
  input  R,
  output Q,
  output NOT_Q
);

  wire nand_3_out, nand_4_out;

  nand nand_1 (Q, nand_3_out, NOT_Q);
  nand nand_2 (NOT_Q, Q, nand_4_out);
  nand nand_3 (nand_3_out, S, C);
  nand nand_4 (nand_4_out, C, R);
endmodule

module _1c_NOR_vs_NAND (
);

  wire n1c_nand_1_not_q, n1c_nand_1_q, n1c_nor_1_not_q, n1c_nor_1_q;

  _1c_NOR u_1c_nor_1 (.NOT_Q(n1c_nor_1_not_q), .Q(n1c_nor_1_q), .C(1'b1), .R(1'b1), .S(1'b1));
  _1c_NAND u_1c_nand_1 (.Q(n1c_nand_1_q), .NOT_Q(n1c_nand_1_not_q), .S(1'b1), .C(1'b1), .R(1'b1));

  // Notes on the sheet:
  //   Unterscheiden von NOR und NAND:
  //   NOR ist im illegalen Zustand LOW:
  //   NAND ist im illegalen Zustand HIGH:
endmodule

module _2d_Schaltwerk_Wecker (
  input  BTN_prime_0,
  input  BTN_prime_1,
  output Q0_OUT,
  output Q1_OUT
);

  wire and_1_out, and_2_out, and_3_out, and_4_out, and_5_out, and_6_out, buffer_1_out, buffer_2_out,
       or_1_out, or_2_out, xor_1_out;

  xor xor_1 (xor_1_out, BTN_prime_0, BTN_prime_1);
  buf buffer_1 (buffer_1_out, xor_1_out);
  and and_1 (and_1_out, ~Q0_OUT, BTN_prime_0, ~BTN_prime_1);  // AND_Gate
  and and_2 (and_2_out, Q0_OUT, ~BTN_prime_0, ~BTN_prime_1);  // AND_Gate
  and and_3 (and_3_out, Q0_OUT, BTN_prime_0, BTN_prime_1);
  buf buffer_2 (buffer_2_out, buffer_1_out);
  and and_4 (and_4_out, ~Q1_OUT, ~BTN_prime_0, BTN_prime_1);  // AND_Gate
  and and_5 (and_5_out, Q1_OUT, ~BTN_prime_0, ~BTN_prime_1);  // AND_Gate
  and and_6 (and_6_out, Q1_OUT, BTN_prime_0, BTN_prime_1);
  or or_1 (or_1_out, and_1_out, and_2_out, and_3_out);
  or or_2 (or_2_out, and_4_out, and_5_out, and_6_out);
  D_Flip_Flop d_ff_1 (.clk(buffer_2_out), .D(or_1_out), .Q(Q0_OUT), .en(1'b1));  // open: Qn, preset, reset
  D_Flip_Flop d_ff_2 (.clk(buffer_2_out), .D(or_2_out), .Q(Q1_OUT), .en(1'b1));  // open: Qn, preset, reset
endmodule
